# Fritzing sketch attiny_pcb (saved by Fritzing 0.9.3b)
circuit board: 3.4709cm x 5.57875cm
breadboards: 1

parts:
  LED3 = smd LED [color="Red (633nm)" package="0603 [SMD]"]
  R1 = Resistor [tolerance=±5% resistance=220 package="2010 [SMD]"]
  U3 = attiny85 [package=dip]
  PIR2 = PIR sensor
  BAT1 = Battery Holders [package=battcon_245mm_pth]

nets:
  N1: LED3.cathode, R1.Pin_1
  N2: LED3.anode, U3.Pin_5
  N3: R1.Pin_0, U3.Pin_4, PIR2.GND, BAT1.-
  N4: U3.Pin_7, PIR2.SIG
  N5: U3.Pin_8, PIR2.VDD, BAT1.+
