# Fritzing sketch space_interface_schematics (saved by Fritzing 0.9.2b)
perfboards: 1

parts:
  Part1 = Arduino Uno (Rev3)
  LED1 = smd LED [color="Red (633nm)" package="0805 [SMD]"]
  LED2 = smd LED [color="Red (633nm)" package="0805 [SMD]"]
  R1 = Resistor [tolerance=±5% resistance=220 package="1206 [SMD]"]
  R2 = Resistor [tolerance=±5% resistance=220 package="1206 [SMD]"]
  R3 = Resistor [tolerance=±5% resistance=220 package="1206 [SMD]"]
  LED3 = smd LED [color="Green (555nm)" package="0805 [SMD]"]

nets:
  N1: Part1.D2, LED1.anode
  N2: Part1.D3_PWM, LED2.anode
  N3: Part1.D4, LED3.anode
  N4: Part1.GND, R1.Pin_0, R2.Pin_0, R3.Pin_0
  N5: LED1.cathode, R1.Pin_1
  N6: LED2.cathode, R3.Pin_1
  N7: R2.Pin_1, LED3.cathode
